# Fritzing sketch Schema ESP32_AD8232 (saved by Fritzing 1.0.1rc)
breadboards: 2

parts:
  U1 = ESP32-38PinWide [part_number=ESP32-38PinWide]
  Mod1 = AD8232 HeartRate Monitor [part_number=SEN-12650]

nets:
  N1: U1.3.3, Mod1.3.3v
  N2: U1.GPIO36, Mod1.OUTPUT
  N3: U1.GPIO32, Mod1.LO+
  N4: U1.GPIO33, Mod1.LO-
  GND: U1.GND, Mod1.GND

custom parts:
  ESP32-38PinWide: Generic 38-Pin ESP32 with wide format (only access to one side of pins on a breadboard) based on Stephen Lilley's HiLetgo ESP-WROOM-32 ESP32 ESP-32S Development Board.
  AD8232 HeartRate Monitor: Sparkfun single lead heart rate monitor - Ad8232.
